// Logisim project project2mips.circ as structural Verilog: 10 circuits, main circuit FeedOpR
module FeedOpR (
  input  F3,
  input  F5,
  input  F2,
  input  F1,
  input  F0,
  output [1:0] MOV,
  output [1:0] SLT,
  output Op3,
  output Op2,
  output Op1,
  output Op0
);

  wire and_1_out, and_2_out, and_3_out, and_4_out, and_5_out, and_6_out, and_7_out, and_8_out, not_1_out,
       not_2_out, not_3_out, not_4_out, not_5_out, not_6_out, not_7_out;

  not not_1 (not_1_out, F5);
  not not_2 (not_2_out, F1);
  not not_3 (not_3_out, F5);
  not not_4 (not_4_out, F1);
  not not_5 (not_5_out, F2);
  not not_6 (not_6_out, F5);
  not not_7 (not_7_out, F2);
  and and_1 (and_1_out, not_1_out, not_2_out, F0);
  and and_2 (and_2_out, F5, F2);
  and and_3 (and_3_out, not_3_out, F0);
  and and_4 (and_4_out, not_4_out, F0);
  and and_5 (and_5_out, F5, F0);
  and and_6 (and_6_out, F5, not_5_out, F1);
  and and_7 (and_7_out, not_6_out, F0);
  and and_8 (and_8_out, F5, not_7_out, F1);
  and and_9 (MOV[1], ~F5, F3);  // AND_Gate
  and and_10 (SLT[1], F3, F5);
  or or_1 (Op3, and_1_out, and_2_out);
  or or_2 (Op2, and_3_out, F1);
  or or_3 (Op1, and_4_out, and_5_out, and_6_out);
  or or_4 (Op0, and_7_out, and_8_out);

  assign MOV[0] = F0;
  assign SLT[0] = F0;
endmodule

module FeedOpI (
  input  F2,
  input  F1,
  input  F0,
  output [1:0] SLT,
  output Op3,
  output Op2,
  output Op1,
  output Op0
);

  wire and_2_out, and_3_out, and_4_out, and_5_out, and_6_out, and_7_out, and_8_out, and_9_out, not_1_out,
       not_2_out, not_3_out, not_4_out, not_5_out, not_6_out, not_7_out, not_8_out, not_9_out, not_10_out,
       not_11_out;

  and and_1 (SLT[1], ~F2, F1);  // AND_Gate
  not not_1 (not_1_out, F1);
  not not_2 (not_2_out, F0);
  not not_3 (not_3_out, F1);
  not not_4 (not_4_out, F0);
  not not_5 (not_5_out, F2);
  not not_6 (not_6_out, F0);
  not not_7 (not_7_out, F2);
  not not_8 (not_8_out, F0);
  not not_9 (not_9_out, F1);
  not not_10 (not_10_out, F2);
  and and_2 (and_2_out, F1, F0);
  and and_3 (and_3_out, not_1_out, not_2_out);
  and and_4 (and_4_out, F2, not_3_out);
  and and_5 (and_5_out, F2, not_4_out);
  and and_6 (and_6_out, not_5_out, not_6_out);
  and and_7 (and_7_out, not_7_out, F1);
  and and_8 (and_8_out, F1, not_8_out);
  not not_11 (not_11_out, F2);
  and and_9 (and_9_out, not_9_out, F0);
  or or_1 (Op0, not_10_out, and_2_out);
  or or_2 (Op3, and_3_out, and_4_out, and_5_out);
  or or_3 (Op2, and_6_out, and_7_out, and_8_out);
  or or_4 (Op1, not_11_out, and_9_out);

  assign SLT[0] = F0;
endmodule

module Memory (
  input  [31:0] ALUinput,
  input  [31:0] Bin,
  input  CtrlIorR,
  input  [31:0] PCPlus4,
  input  [4:0] rW,
  input  WE,
  output [31:0] WALU,
  output [31:0] Wmemory,
  output CtrlOut,
  output [4:0] rWout,
  output WEout
);

  // MIPS_RAM mips_ram_1: pin names not known; wires that end beside it: Bin, Wmemory

  assign CtrlOut = CtrlIorR;
  assign rWout = rW;
  assign WALU = ALUinput;
  assign WEout = WE;
endmodule

module Writeback (
  input  [31:0] WALU,
  input  [31:0] Wmemory,
  input  CtrlIorR,
  input  [4:0] rW,
  input  WE,
  output [31:0] WData,
  output [4:0] rWout,
  output WEout
);

  Multiplexer #(.width(32), .enable("false")) multiplexer_1 (.in1(Wmemory), .sel(CtrlIorR));  // open: in0, out

  assign rWout = rW;
  assign WData = WALU;
  assign WEout = WE;
endmodule

module InstructionFetch (
  input  Clock,
  output [31:0] PCPlus4
);

  wire [31:2] incrementer_1_p2;

  Register #(.width(32)) register_1 (.D({incrementer_1_p2, PCPlus4[1:0]}), .clk(Clock), .Q(PCPlus4));  // open: en, clr
  // Incrementer #(.width(30)) incrementer_1: pin names not known; wires that end beside it: PCPlus4[31:2], incrementer_1_p2
endmodule

module Decode (
  input  [31:0] inst,
  input  [31:0] PCPlus4,
  output [4:0] rA,
  output [4:0] rB,
  output [7:0] Op,
  output [31:0] Imm,
  output [4:0] rW,
  output [1:0] Ctrl,
  output [3:0] MovSlt,
  output [31:0] PCPlus4out,
  output WE
);

  wire not_1_out;
  wire [1:0] bit_extender_3_out, feedopi_1_slt, feedopr_1_mov, feedopr_1_slt;
  wire [31:0] bit_extender_1_out, bit_extender_2_out;

  FeedOpI feedopi_1 (
    .F2(inst[28]), .F1(inst[27]), .F0(inst[26]), .SLT(feedopi_1_slt), .Op3(Op[3]), .Op2(Op[2]), .Op1(Op[1]),
    .Op0(Op[0]));
  FeedOpR feedopr_1 (
    .F3(inst[3]), .F5(inst[5]), .F2(inst[2]), .F1(inst[1]), .F0(inst[0]), .MOV(feedopr_1_mov),
    .SLT(feedopr_1_slt), .Op3(Op[7]), .Op2(Op[6]), .Op1(Op[5]), .Op0(Op[4]));
  Multiplexer #(.width(5), .enable("false")) multiplexer_1 (
    .in0(inst[15:11]), .in1(inst[20:16]), .out(rW), .sel(inst[29]));
  assign bit_extender_1_out = {{16{inst[15]}}, inst[15:0]};  // Bit_Extender bit_extender_1
  assign bit_extender_2_out = {{16{1'b0}}, inst[15:0]};  // Bit_Extender bit_extender_2
  Multiplexer #(.width(32), .enable("false")) multiplexer_2 (
    .in0(bit_extender_1_out), .in1(bit_extender_2_out), .out(Imm), .sel(inst[28]));
  not not_1 (not_1_out, inst[29]);
  assign bit_extender_3_out = {{1{1'b0}}, not_1_out};  // Bit_Extender bit_extender_3
  Multiplexer #(.width(2), .enable("false")) multiplexer_3 (
    .in0(feedopr_1_slt), .in1(feedopi_1_slt), .out(MovSlt[3:2]), .sel(inst[29]));
  WriteEnable writeenable_1 (
    .Op5(inst[31]), .Op3(inst[29]), .Op2(inst[28]), .Op1(inst[27]), .Op0(inst[26]), .F3(inst[3]),
    .F1(inst[1]), .X(WE));
  Multiplexer #(.width(2), .enable("false")) multiplexer_4 (
    .in0(feedopr_1_mov), .in1(bit_extender_3_out), .out(MovSlt[1:0]), .sel(inst[29]));

  assign Ctrl = {inst[2], inst[29]};
  assign PCPlus4out = PCPlus4;
  assign rA = inst[25:21];
  assign rB = inst[20:16];

  // Notes on the sheet:
  //   OpI
  //   OpR
  //   CtrlIorR
  //   ShiftLorVar
  //   Slt
  //   Mov
endmodule

module MIPS (
  output out_1
);

  wire clock_1_out, CtrlIorR2_q, CtrlIorR_q, decode_1_we, execute_1_ctrlout, execute_1_we, memory_1_ctrlout,
       memory_1_weout, not_1_out, WE2_q, WE3_q, WE_q;
  wire [1:0] Ctrl_q, decode_1_ctrl, forwarding_1_a_forward, forwarding_1_b_forward;
  wire [3:0] decode_1_movslt, MovSlt_q;
  wire [4:0] decode_1_ra, decode_1_rb, decode_1_rw, execute_1_rwout, memory_1_rwout, rA_q, rB_q,
       registerfile_1_p4, rW2_q, rW3_q, rW_q;
  wire [7:0] decode_1_op, Op_q;
  wire [31:0] A_q, ALU_q, B_q, Bin_q, CPlus4_q, decode_1_imm, decode_1_pcplus4out, execute_1_pcplus4out,
       execute_1_rt, execute_1_walu, Imm_q, Inst_q, instructionfetch_1_pcplus4, memory_1_walu,
       memory_1_wmemory, mipsprogramrom_1_p2, PCPlus4_q, PPlus4_q, registerfile_1_p1, registerfile_1_p7,
       registerfile_1_p8, WALU_q, Wmemory_q;

  Clock clock_1 (.out(clock_1_out));
  InstructionFetch instructionfetch_1 (.Clock(clock_1_out), .PCPlus4(instructionfetch_1_pcplus4));
  // MIPSProgramROM mipsprogramrom_1: pin names not known; wires that end beside it: instructionfetch_1_pcplus4, mipsprogramrom_1_p2
  Register #(.width(32)) Inst (.D(mipsprogramrom_1_p2), .clk(clock_1_out), .Q(Inst_q));  // open: en, clr
  Register #(.width(32)) PCPlus4 (.D(instructionfetch_1_pcplus4), .clk(clock_1_out), .Q(PCPlus4_q));  // open: en, clr
  not not_1 (not_1_out, clock_1_out);
  Decode decode_1 (
    .inst(Inst_q), .PCPlus4(PCPlus4_q), .rA(decode_1_ra), .rB(decode_1_rb), .Op(decode_1_op),
    .Imm(decode_1_imm), .rW(decode_1_rw), .Ctrl(decode_1_ctrl), .MovSlt(decode_1_movslt),
    .PCPlus4out(decode_1_pcplus4out), .WE(decode_1_we));
  // RegisterFile registerfile_1: pin names not known; wires that end beside it: registerfile_1_p1, not_1_out, out_1, registerfile_1_p4, decode_1_ra, decode_1_rb, registerfile_1_p7, registerfile_1_p8
  Register #(.width(32)) A (.D(registerfile_1_p7), .clk(clock_1_out), .Q(A_q));  // open: en, clr
  Register #(.width(32)) B (.D(registerfile_1_p8), .clk(clock_1_out), .Q(B_q));  // open: en, clr
  Register #(.width(32)) Imm (.D(decode_1_imm), .clk(clock_1_out), .Q(Imm_q));  // open: en, clr
  Register Op (.D(decode_1_op), .clk(clock_1_out), .Q(Op_q));  // open: en, clr
  Register #(.width(2)) Ctrl (.D(decode_1_ctrl), .clk(clock_1_out), .Q(Ctrl_q));  // open: en, clr
  Register #(.width(4)) MovSlt (.D(decode_1_movslt), .clk(clock_1_out), .Q(MovSlt_q));  // open: en, clr
  Register #(.width(5)) rW (.D(decode_1_rw), .clk(clock_1_out), .Q(rW_q));  // open: en, clr
  Register #(.width(32)) PPlus4 (.D(decode_1_pcplus4out), .clk(clock_1_out), .Q(PPlus4_q));  // open: en, clr
  Register #(.width(5)) rA (.D(decode_1_ra), .clk(clock_1_out), .Q(rA_q));  // open: en, clr
  Register #(.width(5)) rB (.D(decode_1_rb), .clk(clock_1_out), .Q(rB_q));  // open: en, clr
  Register #(.width(1)) WE (.D(decode_1_we), .clk(clock_1_out), .Q(WE_q));  // open: en, clr
  Execute execute_1 (
    .WVal(WALU_q), .MVal(ALU_q), .A(A_q), .B(B_q), .A_forw(forwarding_1_a_forward),
    .B_forw(forwarding_1_b_forward), .Imm(Imm_q), .Op(Op_q), .Ctrl(Ctrl_q), .MovSlt(MovSlt_q), .rW(rW_q),
    .PCPlus4(PPlus4_q), .WEin(WE_q), .WALU(execute_1_walu), .Rt(execute_1_rt), .CtrlOut(execute_1_ctrlout),
    .rWout(execute_1_rwout), .PCPlus4out(execute_1_pcplus4out), .WE(execute_1_we));
  Forwarding forwarding_1 (
    .Writeback_we(WE3_q), .Writeback_Rd(rW3_q), .Ra(rA_q), .Execute_we(WE_q), .Mem_Rd(rW2_q), .Rb(rB_q),
    .A_forward(forwarding_1_a_forward), .B_forward(forwarding_1_b_forward));
  Register #(.width(32)) ALU (.D(execute_1_walu), .clk(clock_1_out), .Q(ALU_q));  // open: en, clr
  Register #(.width(32)) Bin (.D(execute_1_rt), .clk(clock_1_out), .Q(Bin_q));  // open: en, clr
  Register #(.width(1)) CtrlIorR (.D(execute_1_ctrlout), .clk(clock_1_out), .Q(CtrlIorR_q));  // open: en, clr
  Register #(.width(5)) rW2 (.D(execute_1_rwout), .clk(clock_1_out), .Q(rW2_q));  // open: en, clr
  Register #(.width(32)) CPlus4 (.D(execute_1_pcplus4out), .clk(clock_1_out), .Q(CPlus4_q));  // open: en, clr
  Register #(.width(1)) WE2 (.D(execute_1_we), .clk(clock_1_out), .Q(WE2_q));  // open: en, clr
  Memory memory_1 (
    .ALUinput(ALU_q), .Bin(Bin_q), .CtrlIorR(CtrlIorR_q), .PCPlus4(CPlus4_q), .rW(rW2_q), .WE(WE2_q),
    .WALU(memory_1_walu), .Wmemory(memory_1_wmemory), .CtrlOut(memory_1_ctrlout), .rWout(memory_1_rwout),
    .WEout(memory_1_weout));
  Register #(.width(32)) WALU (.D(memory_1_walu), .clk(clock_1_out), .Q(WALU_q));  // open: en, clr
  Register #(.width(32)) Wmemory (.D(memory_1_wmemory), .clk(clock_1_out), .Q(Wmemory_q));  // open: en, clr
  Register #(.width(1)) CtrlIorR2 (.D(memory_1_ctrlout), .clk(clock_1_out), .Q(CtrlIorR2_q));  // open: en, clr
  Register #(.width(5)) rW3 (.D(memory_1_rwout), .clk(clock_1_out), .Q(rW3_q));  // open: en, clr
  Register #(.width(1)) WE3 (.D(memory_1_weout), .clk(clock_1_out), .Q(WE3_q));  // open: en, clr
  Writeback writeback_1 (
    .WALU(WALU_q), .Wmemory(Wmemory_q), .CtrlIorR(CtrlIorR2_q), .rW(rW3_q), .WE(WE3_q),
    .WData(registerfile_1_p1), .rWout(registerfile_1_p4), .WEout(out_1));

  // Notes on the sheet:
  //   contents of mipsprogramrom_1 (hex, n*v repeats v):
  //   ADDIU $10,$0,1 ADDU $11,$10,$10 ADDU $12,$11,$10 SUBU $9,$13,$12  #Tests immediate and variable
  //   shifting (both arithmetic and logical) SLLV $1,$11,$10 SRLV $2,$11,$10 SRAV $3,$11,$10 SLL $4,$11,1
  //   SRL $5,$11,1 SRA $6,$11,1  #Tests loading LUI $7,2 LUI $9,15   #Logical operators (immediate and
  //   variable) XOR $14,$13,$12 XORI $14,$13,1 OR $14,$13,$12 NOR $14,$13,$12 ORI $16,$13,3 AND
  //   $15,$13,$12 ANDI $17,$13,3  #MOVN/MOVZ testing (notice that we will attempt loading  #into the 0
  //   register, but this will set WE to 0) MOVN $25,$10,$9 MOVN $26,$10,$11 MOVN $27,$10,$0 MOVN $0,$9,$9
  //   MOVZ $0,$9,$0 MOVZ $0,$9,$0 MOVZ $28,$10,$11 MOVZ $29,$10,$9  #SLT testing SLT $12,$9,$10 SLTI
  //   $13,$9,5 SLTU $12,$9,$10 SLTIU $15,$9,5 SLTI $14,$9,5 SLT $14,$10,$9
endmodule

module Execute (
  input  [31:0] WVal,
  input  [31:0] MVal,
  input  [31:0] A,
  input  [31:0] B,
  input  [1:0] A_forw,
  input  [1:0] B_forw,
  input  [31:0] Imm,
  input  [7:0] Op,
  input  [1:0] Ctrl,
  input  [3:0] MovSlt,
  input  [4:0] rW,
  input  [31:0] PCPlus4,
  input  WEin,
  output [31:0] WALU,
  output [31:0] Rt,
  output CtrlOut,
  output [4:0] rWout,
  output [31:0] PCPlus4out,
  output WE
);

  wire and_1_out, and_2_out, comparator_1_lt, comparator_2_lt, multiplexer_10_out, nor_1_out, not_2_out,
       or_1_out, xor_1_out;
  wire [3:0] multiplexer_6_out;
  wire [3:3] not_1_out;
  wire [4:0] mips_alu_1_p6, multiplexer_7_out;
  wire [31:0] bit_extender_1_out, bit_extender_2_out, multiplexer_1_out, multiplexer_2_out,
       multiplexer_3_out, multiplexer_5_out, multiplexer_9_out, multiplexer_11_out, multiplexer_12_out,
       multiplexer_13_out, undriven;

  Multiplexer #(.width(32), .enable("false")) multiplexer_1 (
    .in0(A), .in1(WVal), .out(multiplexer_1_out), .sel(A_forw[1]));
  Multiplexer #(.width(32), .enable("false")) multiplexer_2 (
    .in0(B), .in1(WVal), .out(multiplexer_2_out), .sel(B_forw[1]));
  Multiplexer #(.width(32), .enable("false")) multiplexer_3 (
    .in0(multiplexer_1_out), .in1(MVal), .out(multiplexer_3_out), .sel(A_forw[0]));
  Multiplexer #(.width(32), .enable("false")) multiplexer_4 (
    .in0(multiplexer_2_out), .in1(MVal), .out(Rt), .sel(B_forw[0]));
  not not_1 (not_1_out[3], Ctrl[0]);
  Multiplexer #(.width(32), .enable("false")) multiplexer_5 (
    .in0(Rt), .in1(Imm), .out(multiplexer_5_out), .sel(Ctrl[0]));
  Multiplexer #(.width(4), .enable("false")) multiplexer_6 (
    .in0(Op[7:4]), .in1(Op[3:0]), .out(multiplexer_6_out), .sel(Ctrl[0]));
  Multiplexer #(.width(5), .enable("false")) multiplexer_7 (
    .in0(Imm[10:6]), .in1(multiplexer_3_out[4:0]), .out(multiplexer_7_out), .sel(Ctrl[1]));
  // Mips_ALU mips_alu_1: pin names not known; wires that end beside it: Imm[15:11], Op[7:4], multiplexer_3_out, multiplexer_5_out, multiplexer_6_out, mips_alu_1_p6
  Multiplexer #(.width(5), .enable("false")) multiplexer_8 (
    .in0(multiplexer_7_out), .in1({Ctrl[0], {4{not_1_out[3]}}}), .out(mips_alu_1_p6), .sel(Ctrl[0]));
  nor nor_1 (nor_1_out, Rt[15], Rt[0], Rt[1], Rt[2], Rt[3], Rt[4], Rt[5], Rt[6], Rt[7], Rt[8], Rt[9], Rt[10], Rt[11], Rt[12], Rt[13], Rt[14], Rt[16], Rt[17], Rt[18], Rt[19], Rt[20], Rt[21], Rt[22], Rt[23], Rt[24], Rt[25], Rt[26], Rt[27], Rt[28], Rt[29], Rt[30], Rt[31]);
  xor xor_1 (xor_1_out, nor_1_out, MovSlt[0]);
  Comparator #(.width(32)) comparator_1 (.a(undriven), .b(bit_extender_2_out), .lt(comparator_1_lt));  // open: gt, eq
  Comparator #(.width(32), .mode("unsigned")) comparator_2 (
    .a(undriven), .b(bit_extender_2_out), .lt(comparator_2_lt));  // open: gt, eq
  Multiplexer #(.width(32)) multiplexer_9 (
    .in0(Imm), .in1(multiplexer_3_out), .out(multiplexer_9_out), .sel(xor_1_out), .en(and_1_out));
  Multiplexer #(.enable("false")) multiplexer_10 (
    .in0(comparator_1_lt), .in1(comparator_2_lt), .out(multiplexer_10_out), .sel(MovSlt[2]));
  not not_2 (not_2_out, MovSlt[3]);
  and and_1 (and_1_out, MovSlt[1], xor_1_out);
  assign bit_extender_1_out = {{31{1'b0}}, multiplexer_10_out};  // Bit_Extender bit_extender_1
  assign bit_extender_2_out = {{31{1'b0}}, not_2_out};  // Bit_Extender bit_extender_2
  Multiplexer #(.width(32), .enable("false")) multiplexer_11 (
    .in0(Imm), .in1(Rt), .out(multiplexer_11_out), .sel(Ctrl[0]));
  Multiplexer #(.width(32), .enable("false")) multiplexer_12 (
    .in0(multiplexer_11_out), .in1(bit_extender_1_out), .out(multiplexer_12_out), .sel(MovSlt[3]));
  Multiplexer #(.width(32), .enable("false")) multiplexer_13 (
    .in0(multiplexer_12_out), .in1(multiplexer_9_out), .out(multiplexer_13_out), .sel(and_2_out));
  and and_2 (and_2_out, ~Imm[5], ~Ctrl[0]);  // AND_Gate
  Multiplexer #(.width(32), .enable("false")) multiplexer_14 (
    .in0(undriven), .in1(multiplexer_13_out), .out(WALU), .sel(or_1_out));
  or or_1 (or_1_out, MovSlt[1], MovSlt[3]);

  assign CtrlOut = Ctrl[0];
  assign PCPlus4out = PCPlus4;
  assign rWout = rW;
  assign WE = WEin;

  // Notes on the sheet:
  //   A
  //   B
  //   Imm
  //   OpI
  //   OpR
  //   CtrlIorR
  //   ShiftLorVar
  //   Mov
  //   Slt
endmodule

module Forwarding (
  input  Writeback_we,
  input  [4:0] Writeback_Rd,
  input  [4:0] Ra,
  input  Execute_we,
  input  [4:0] Mem_Rd,
  input  [4:0] Rb,
  output [1:0] A_forward,
  output [1:0] B_forward
);

  wire and_1_out, and_2_out, and_3_out, and_4_out, or_1_out, or_2_out, or_3_out, or_4_out;
  wire [4:0] xnor_1_out, xnor_2_out, xnor_3_out, xnor_4_out;

  assign xnor_1_out = ~(Writeback_Rd ^ Ra);  // XNOR_Gate xnor_1, 5 bits wide
  assign xnor_2_out = ~(Mem_Rd ^ Ra);  // XNOR_Gate xnor_2, 5 bits wide
  assign xnor_3_out = ~(Writeback_Rd ^ Rb);  // XNOR_Gate xnor_3, 5 bits wide
  assign xnor_4_out = ~(Mem_Rd ^ Rb);  // XNOR_Gate xnor_4, 5 bits wide
  or or_1 (or_1_out, Writeback_Rd[0], Writeback_Rd[1], Writeback_Rd[2], Writeback_Rd[3], Writeback_Rd[4]);
  and and_1 (and_1_out, xnor_1_out[0], xnor_1_out[1], xnor_1_out[2], xnor_1_out[3], xnor_1_out[4]);
  or or_2 (or_2_out, Mem_Rd[0], Mem_Rd[1], Mem_Rd[2], Mem_Rd[3], Mem_Rd[4]);
  and and_2 (and_2_out, xnor_2_out[0], xnor_2_out[1], xnor_2_out[2], xnor_2_out[3], xnor_2_out[4]);
  or or_3 (or_3_out, Writeback_Rd[0], Writeback_Rd[1], Writeback_Rd[2], Writeback_Rd[3], Writeback_Rd[4]);
  and and_3 (and_3_out, xnor_3_out[0], xnor_3_out[1], xnor_3_out[2], xnor_3_out[3], xnor_3_out[4]);
  or or_4 (or_4_out, Mem_Rd[0], Mem_Rd[1], Mem_Rd[2], Mem_Rd[3], Mem_Rd[4]);
  and and_4 (and_4_out, xnor_4_out[0], xnor_4_out[1], xnor_4_out[2], xnor_4_out[3], xnor_4_out[4]);
  and and_5 (A_forward[1], Writeback_we, or_1_out, and_1_out);
  and and_6 (A_forward[0], Execute_we, or_2_out, and_2_out);
  and and_7 (B_forward[1], Writeback_we, or_3_out, and_3_out);
  and and_8 (B_forward[0], Execute_we, or_4_out, and_4_out);
endmodule

module WriteEnable (
  input  Op5,
  input  Op3,
  input  Op2,
  input  Op1,
  input  Op0,
  input  F3,
  input  F1,
  output X
);

  wire and_1_out, and_2_out, or_1_out, or_2_out;

  and and_1 (and_1_out, ~Op1, ~Op2, ~Op3, F3, ~F1);  // AND_Gate
  or or_1 (or_1_out, Op2, Op1, and_1_out, Op0);
  and and_2 (and_2_out, ~Op5, ~Op3, or_1_out);  // AND_Gate
  or or_2 (or_2_out, Op5, and_2_out);
  not not_1 (X, or_2_out);
endmodule
